# Fritzing sketch Esquema general (saved by Fritzing 1.0.5)
breadboards: 1

parts:
  Parte1 = Arduino Uno (Rev3)
  DHT1 = DHT11 Humitidy and Temperature Sensor
  M1 = DFR sen0308 [package=THT]
  LCD2 = LCD screen
  LCM1602_IIC2 = LCM1602 IIC [part_number="LCM1602 IIC" chip_label="LCM1602 IIC" package="DIP (Dual Inline) [THT]"]

nets:
  N1: Parte1.A0, M1.pin2
  GND: Parte1.GND, DHT1.GND, M1.pin1, M1.pin3, LCM1602_IIC2.GND
  N2: Parte1.A4/SDA, LCM1602_IIC2.SDA
  N3: Parte1.A5/SCL, LCM1602_IIC2.SCL
  N4: Parte1.D2, DHT1.DATA
  N5: Parte1.3V3, M1.pin4
  5V: Parte1.5V, DHT1.VDD, LCM1602_IIC2.VCC
  N6: LCD2.DB1, LCM1602_IIC2.D1
  N7: LCD2.DB2, LCM1602_IIC2.D2
  N8: LCD2.DB3, LCM1602_IIC2.D3
  N9: LCD2.DB4, LCM1602_IIC2.D4
  N10: LCD2.DB5, LCM1602_IIC2.D5
  N11: LCD2.DB6, LCM1602_IIC2.D6
  N12: LCD2.DB7, LCM1602_IIC2.D7
  N13: LCD2.LED+, LCM1602_IIC2.A
  N14: LCD2.LED-, LCM1602_IIC2.K
  N15: LCM1602_IIC2.LED_A, LCM1602_IIC2.LED_B

custom parts:
  DHT11 Humitidy and Temperature Sensor: DHT11 Humidity and Temperature Sensor
  DFR sen0308: This is a new type of waterproof soil moisture sensor introduced by DFRobot. Compared with the previous version of the soil moisture sensor, it has increased waterproof performance, optimized corrosion resistance, increased plate length and optimized circuit performance. Compared with the resistive sensor, the capacitive soil moisture sensor solves the problem that the resistive sensor is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
  LCM1602 IIC: I2C-Module to use a 1602 or 2004 LCD on with the wire.h libory Serial LCD Modul
